# Fritzing sketch Untitled Sketch (saved by Fritzing 0.9.3b)

parts:
  Part1 = Arduino Uno (Rev3)
  LED1 = LED - 5mm [color="Red (633nm)" package="5 mm [THT]"]
  J1 = Piezo Speaker
  R1 = Photocell (LDR) [package=THT]
  LED2 = smd LED [color="Red (633nm)" package="0603 [SMD]"]
  VCC1 = Battery block 9V  # not connected

nets:
  N1: Part1.A1, R1.pin_1
  N2: Part1.D9_PWM, J1.pin2
  N3: Part1.D10_PWM/SS, LED2.anode
  N4: Part1.D13/SCK, LED1.anode
  N5: Part1.GND, LED1.cathode, J1.pin1, R1.pin_0, LED2.cathode
