# Fritzing sketch Untitled Sketch (saved by Fritzing 0.9.3b)

parts:
  BAT1 = BC9VPC [package=bc9vpc]  # not connected
  Part1 = Arduino Uno (Rev3)
  LCD1 = LCD screen
  LED1 = LED - 5mm [color="Red (633nm)" package="5 mm [THT]"]
  J1 = Piezo Speaker
  R1 = TRIMPOT [package=trimpot_pth_s3_lock]
  RHT1 = Humidity and Temperature Sensor RHT03
  R2 = Resistor [tolerance=±5% resistance=220 package="0805 [SMD]"]  # not connected
  U1 = GAS_SENSOR [package=mq-3]

nets:
  N1: Part1.A0, U1.B1
  N2: Part1.D8, J1.pin2
  N3: Part1.D9_PWM, LED1.anode
  N4: Part1.D11_PWM/MOSI, LCD1.E
  N5: Part1.D12/MISO, LCD1.RS
  N6: Part1.GND, J1.pin1, RHT1.GND_1
  N7: Part1.D2, LCD1.DB7
  N8: Part1.D3_PWM, LCD1.DB6
  N9: Part1.D4, LCD1.DB5
  N10: Part1.D5_PWM, LCD1.DB4
  N11: Part1.D7, RHT1.Vcc
  N12: Part1.5V, RHT1.GND_2
  N13: LCD1.V0, R1.WIPER
